// Logisim project Lab3_Procesador_Monociclo.circ as structural Verilog: 5 circuits, main circuit main
module main (
);

  wire [31:0] ifetch_1_instruction;

  IFetch ifetch_1 (.Instruction(ifetch_1_instruction));  // open: nextPC, CLK, Reset, PCplus4
  ISplit isplit_1 (.Instruction(ifetch_1_instruction));  // open: immediate, address, funct, shamt, rd, rt, rs, opcode
  RegFile regfile_1 ();  // open: ReadReg1, ReadReg2, WriteRegister, WriteData, CLK, RegWrite, Reset, ReadData1, ReadData2
  ALU alu_1 ();  // open: A, B, ALUOperation, zero, ALUResult
endmodule

module IFetch (
  input  [31:0] nextPC,
  input  CLK,
  input  Reset,
  output [31:0] PCplus4,
  output [31:0] Instruction
);

  wire [1:0] register_1_q, register_1_q_2, register_1_q_3, register_1_q_4, register_1_q_5, register_1_q_6,
       register_1_q_7, register_1_q_8, register_1_q_9, register_1_q_10, register_1_q_11, register_1_q_12,
       register_1_q_13, register_1_q_14, register_1_q_15, register_1_q_16;

  Register #(.width(32)) register_1 (
    .D(nextPC), .clk(CLK),
    .Q({register_1_q_8, register_1_q_7, register_1_q_6, register_1_q_5, register_1_q_4, register_1_q_3, register_1_q_2, register_1_q_16, register_1_q_15, register_1_q_14, register_1_q_13, register_1_q_12, register_1_q_11, register_1_q_10, register_1_q_9, register_1_q}),
    .clr(Reset));  // open: en
  Adder #(.width(32)) adder_1 (
    .a(32'h4),
    .b({register_1_q_8, register_1_q_7, register_1_q_6, register_1_q_5, register_1_q_4, register_1_q_3, register_1_q_2, register_1_q_16, register_1_q_15, register_1_q_14, register_1_q_13, register_1_q_12, register_1_q_11, register_1_q_10, register_1_q_9, register_1_q}),
    .out(PCplus4));  // open: cin, cout
  ROM #(.addrWidth(16), .dataWidth(32)) rom_1 (
    .addr({register_1_q_16, register_1_q_15, register_1_q_14, register_1_q_13, register_1_q_12, register_1_q_11, register_1_q_10, register_1_q_9}),
    .data(Instruction));

  // Notes on the sheet:
  //   contents of rom_1 (hex, n*v repeats v):
  //   dfadfadf
endmodule

module ISplit (
  input  [31:0] Instruction,
  output [15:0] immediate,
  output [25:0] address,
  output [5:0] funct,
  output [4:0] shamt,
  output [4:0] rd,
  output [4:0] rt,
  output [4:0] rs,
  output [5:0] opcode
);


  assign address = Instruction[25:0];
  assign funct = Instruction[5:0];
  assign immediate = Instruction[15:0];
  assign opcode = Instruction[31:26];
  assign rd = Instruction[15:11];
  assign rs = Instruction[25:21];
  assign rt = Instruction[20:16];
  assign shamt = Instruction[10:6];
endmodule

module RegFile (
  input  RegWrite,
  input  [4:0] ReadReg1,
  input  [4:0] ReadReg2,
  input  [4:0] WriteRegister,
  input  [31:0] WriteData,
  input  CLK,
  input  Reset,
  output [31:0] ReadData1,
  output [31:0] ReadData2
);

  wire decoder_1_out0, decoder_1_out1, decoder_1_out2, decoder_1_out3, decoder_1_out4, decoder_1_out5,
       decoder_1_out6, decoder_1_out7, decoder_1_out8, decoder_1_out9, decoder_1_out10, decoder_1_out11,
       decoder_1_out12, decoder_1_out13, decoder_1_out14, decoder_1_out15, decoder_1_out16, decoder_1_out17,
       decoder_1_out18, decoder_1_out19, decoder_1_out20, decoder_1_out21, decoder_1_out22, decoder_1_out23,
       decoder_1_out24, decoder_1_out25, decoder_1_out26, decoder_1_out27, decoder_1_out28, decoder_1_out29,
       decoder_1_out30, decoder_1_out31;
  wire [31:0] a0, a1, a2, a3, at, fp, gp, k0, k1, ra, s0, s1, s2, s3, s4, s5, s6, s7, sp, t0, t1, t2, t3, t4,
       t5, t6, t7, t8, t9, v0, v1, zero;

  Register #(.width(32)) u_a0 (.D(WriteData), .en(decoder_1_out4), .clk(CLK), .Q(a0), .clr(Reset));
  Register #(.width(32)) u_v1 (.D(WriteData), .en(decoder_1_out3), .clk(CLK), .Q(v1), .clr(Reset));
  Register #(.width(32)) u_v0 (.D(WriteData), .en(decoder_1_out2), .clk(CLK), .Q(v0), .clr(Reset));
  Register #(.width(32)) u_at (.D(WriteData), .en(decoder_1_out1), .clk(CLK), .Q(at), .clr(Reset));
  Register #(.width(32)) u_zero (.D(WriteData), .en(decoder_1_out0), .clk(CLK), .Q(zero), .clr(Reset));
  Register #(.width(32)) u_t1 (.D(WriteData), .en(decoder_1_out9), .clk(CLK), .Q(t1), .clr(Reset));
  Register #(.width(32)) u_t0 (.D(WriteData), .en(decoder_1_out8), .clk(CLK), .Q(t0), .clr(Reset));
  Register #(.width(32)) u_a3 (.D(WriteData), .en(decoder_1_out7), .clk(CLK), .Q(a3), .clr(Reset));
  Register #(.width(32)) u_a2 (.D(WriteData), .en(decoder_1_out6), .clk(CLK), .Q(a2), .clr(Reset));
  Register #(.width(32)) u_a1 (.D(WriteData), .en(decoder_1_out5), .clk(CLK), .Q(a1), .clr(Reset));
  Decoder #(.select(5)) decoder_1 (
    .out0(decoder_1_out0), .out1(decoder_1_out1), .out2(decoder_1_out2), .out3(decoder_1_out3),
    .out4(decoder_1_out4), .out5(decoder_1_out5), .out6(decoder_1_out6), .out7(decoder_1_out7),
    .out8(decoder_1_out8), .out9(decoder_1_out9), .out10(decoder_1_out10), .out11(decoder_1_out11),
    .out12(decoder_1_out12), .out13(decoder_1_out13), .out14(decoder_1_out14), .out15(decoder_1_out15),
    .out16(decoder_1_out16), .out17(decoder_1_out17), .out18(decoder_1_out18), .out19(decoder_1_out19),
    .out20(decoder_1_out20), .out21(decoder_1_out21), .out22(decoder_1_out22), .out23(decoder_1_out23),
    .out24(decoder_1_out24), .out25(decoder_1_out25), .out26(decoder_1_out26), .out27(decoder_1_out27),
    .out28(decoder_1_out28), .out29(decoder_1_out29), .out30(decoder_1_out30), .out31(decoder_1_out31),
    .sel(WriteRegister), .en(RegWrite));
  Register #(.width(32)) u_t6 (.D(WriteData), .en(decoder_1_out14), .clk(CLK), .Q(t6), .clr(Reset));
  Register #(.width(32)) u_t5 (.D(WriteData), .en(decoder_1_out13), .clk(CLK), .Q(t5), .clr(Reset));
  Register #(.width(32)) u_t4 (.D(WriteData), .en(decoder_1_out12), .clk(CLK), .Q(t4), .clr(Reset));
  Register #(.width(32)) u_t3 (.D(WriteData), .en(decoder_1_out11), .clk(CLK), .Q(t3), .clr(Reset));
  Register #(.width(32)) u_t2 (.D(WriteData), .en(decoder_1_out10), .clk(CLK), .Q(t2), .clr(Reset));
  Register #(.width(32)) u_s1 (.D(WriteData), .en(decoder_1_out19), .clk(CLK), .Q(s1), .clr(Reset));
  Register #(.width(32)) u_s0 (.D(WriteData), .en(decoder_1_out18), .clk(CLK), .Q(s0), .clr(Reset));
  Register #(.width(32)) u_t9 (.D(WriteData), .en(decoder_1_out17), .clk(CLK), .Q(t9), .clr(Reset));
  Register #(.width(32)) u_t8 (.D(WriteData), .en(decoder_1_out16), .clk(CLK), .Q(t8), .clr(Reset));
  Register #(.width(32)) u_t7 (.D(WriteData), .en(decoder_1_out15), .clk(CLK), .Q(t7), .clr(Reset));
  Register #(.width(32)) u_s6 (.D(WriteData), .en(decoder_1_out24), .clk(CLK), .Q(s6), .clr(Reset));
  Register #(.width(32)) u_s5 (.D(WriteData), .en(decoder_1_out23), .clk(CLK), .Q(s5), .clr(Reset));
  Register #(.width(32)) u_s4 (.D(WriteData), .en(decoder_1_out22), .clk(CLK), .Q(s4), .clr(Reset));
  Register #(.width(32)) u_s3 (.D(WriteData), .en(decoder_1_out21), .clk(CLK), .Q(s3), .clr(Reset));
  Register #(.width(32)) u_s2 (.D(WriteData), .en(decoder_1_out20), .clk(CLK), .Q(s2), .clr(Reset));
  Register #(.width(32)) u_sp (.D(WriteData), .en(decoder_1_out29), .clk(CLK), .Q(sp), .clr(Reset));
  Register #(.width(32)) u_gp (.D(WriteData), .en(decoder_1_out28), .clk(CLK), .Q(gp), .clr(Reset));
  Register #(.width(32)) u_k1 (.D(WriteData), .en(decoder_1_out27), .clk(CLK), .Q(k1), .clr(Reset));
  Register #(.width(32)) u_k0 (.D(WriteData), .en(decoder_1_out26), .clk(CLK), .Q(k0), .clr(Reset));
  Register #(.width(32)) u_s7 (.D(WriteData), .en(decoder_1_out25), .clk(CLK), .Q(s7), .clr(Reset));
  Register #(.width(32)) u_ra (.D(WriteData), .en(decoder_1_out31), .clk(CLK), .Q(ra), .clr(Reset));
  Register #(.width(32)) u_fp (.D(WriteData), .en(decoder_1_out30), .clk(CLK), .Q(fp), .clr(Reset));
  Multiplexer #(.select(5), .width(32)) multiplexer_1 (
    .in0(zero), .in1(at), .in2(v0), .in3(v1), .in4(a0), .in5(a1), .in6(a2), .in7(a3), .in8(t0), .in9(t1),
    .in10(t2), .in11(t3), .in12(t4), .in13(t5), .in14(t6), .in15(t7), .in16(s0), .in17(s1), .in18(s2),
    .in19(s3), .in20(s4), .in21(s5), .in22(s6), .in23(s7), .in24(t8), .in25(t9), .in26(k0), .in27(k1),
    .in28(gp), .in29(sp), .in30(fp), .in31(ra), .out(ReadData1), .sel(ReadReg1));
  Multiplexer #(.select(5), .width(32)) multiplexer_2 (
    .in0(zero), .in1(at), .in2(v0), .in3(v1), .in4(a0), .in5(a1), .in6(a2), .in7(a3), .in8(t0), .in9(t1),
    .in10(t2), .in11(t3), .in12(t4), .in13(t5), .in14(t6), .in15(t7), .in16(s0), .in17(s1), .in18(s2),
    .in19(s3), .in20(s4), .in21(s5), .in22(s6), .in23(s7), .in24(t8), .in25(t9), .in26(k0), .in27(k1),
    .in28(gp), .in29(sp), .in30(fp), .in31(ra), .out(ReadData2), .sel(ReadReg2));

  // Other names for the same wires on the sheet: rr1[4:0] = ReadReg1; rr2[4:0] = ReadReg2; wd[31:0] = WriteData
endmodule

module ALU (
  input  [31:0] A,
  input  [31:0] B,
  input  [2:0] ALUOperation,
  output zero,
  output [31:0] ALUResult
);

  wire [0:0] SLT;
  wire [31:0] ADD, LAND, LNOR, LOR, SUB;

  Adder #(.width(32)) adder_1 (.a(A), .b(B), .out(ADD));  // open: cin, cout
  Subtractor #(.width(32)) subtractor_1 (.a(A), .b(B), .out(SUB));  // open: bin, bout
  assign LAND = A & B;  // AND_Gate and_1, 32 bits wide
  assign LOR = A | B;  // OR_Gate or_1, 32 bits wide
  assign LNOR = ~LOR;  // NOT_Gate not_1, 32 bits wide
  Comparator #(.width(32)) comparator_1 (.a(A), .b(B), .lt(SLT[0]));  // open: gt, eq
  Multiplexer #(.select(3), .width(32)) multiplexer_1 (
    .in0(ADD), .in1(SUB), .in2(LAND), .in3(LOR), .in4(LNOR), .in5({{31{1'b0}}, SLT[0]}), .out(ALUResult),
    .sel(ALUOperation));  // open: in6, in7
  Comparator #(.width(32)) comparator_2 (.a({32{1'b0}}), .b(ALUResult), .eq(zero));  // open: gt, lt
endmodule
